# Fritzing sketch switch_and_led (saved by Fritzing 0.9.2b)
circuit board: 1.88579cm x 1.67126cm
breadboards: 1

parts:
  SWITCH = Toggle Switch [package=THT]
  LED = LED - 5mm [color="Red (633nm)" package="5 mm [THT]"]
  R1 = Resistor [tolerance=±5% resistance=220 package=THT]
  POWER = female pin header, 2 pins [form="♀ (female)"]

nets:
  N1: SWITCH.COM, POWER.pin2
  N2: SWITCH.L2, R1.Pin_0
  N3: LED.cathode, POWER.pin1
  N4: LED.anode, R1.Pin_1

notes:
  {
  "attributes": {
  "PCB": {"parameters": {"pcbHeight": "1.2mm"} },
  "LED": {"parameters": {"distanceFromPCB": "1mm", "drillDepth": "50mm"} },
  "SWITCH": {"parameters": { "drillDepth": "50mm"} }
  }
  }
