# Fritzing sketch switch_and_led_advanced (saved by Fritzing 0.9.2b)
circuit board: 1.88579cm x 1.67126cm
circuit board: 1.88579cm x 1.67126cm
breadboards: 1

parts:
  SWITCH = Toggle Switch [package=THT]
  LED = LED - 5mm [color="Red (633nm)" package="5 mm [THT]"]
  R1 = Resistor [tolerance=±5% resistance=220 package=THT]
  POWER = female pin header, 2 pins [form="♀ (female)"]
  SWITCH1 = Toggle Switch [package=THT]
  LED1 = LED - 5mm [color="Red (633nm)" package="5 mm [THT]"]
  R2 = Resistor [tolerance=±5% resistance=220 package=THT]
  POWER1 = female pin header, 2 pins [form="♀ (female)"]

nets:
  N1: SWITCH.COM, POWER.pin2
  N2: SWITCH.L2, R1.Pin_0
  N3: LED.cathode, POWER.pin1
  N4: LED.anode, R1.Pin_1
  N5: SWITCH1.COM, POWER1.pin2
  N6: SWITCH1.L2, R2.Pin_0
  N7: LED1.cathode, POWER1.pin1
  N8: LED1.anode, R2.Pin_1

notes:
  {
  "attributes": {
  "LED": {
  "parameters": {
  "drillDepth": "50mm"
  }
  },
  "LED1": {
  "parameters": {
  "drillDepth": "2cm"
  }
  },
  "PCB": {
  "parameters": {
  "pcbHeight": "1.2mm"
  }
  },
  "PCB1": {
  "parameters": {
  "pcbHeight": "1.2mm"
  }
  }
  },
  "modules": {
  "a": {
  "frames":["part1"], "parts": ["PCB"]
  },
  "b": {
  "frames":["part2"], "parts": ["PCB1"]
  }
  }
  }
