# Fritzing sketch some_buttons_leds_and_a_switch (saved by Fritzing 0.9.1b)
circuit board: 2cm x 3cm
breadboards: 1

parts:
  LED1 = LED - 5mm [color="Red (633nm)" package="5 mm [THT]"]
  S2 = Toggle Switch [package=THT]
  S3 = Pushbutton [package="[THT]"]
  S4 = Pushbutton [package="[THT]"]
  LED2 = LED - 5mm [color="Red (633nm)" package="5 mm [THT]"]
  LED3 = LED - 5mm [color="Red (633nm)" package="5 mm [THT]"]

nets:
  N1: LED1.cathode, S2.COM
  N2: LED1.anode, LED2.anode, LED3.anode
  N3: S2.L1, S3.Pin_3, S3.Pin_4, S4.Pin_3, S4.Pin_4, LED3.cathode
  N4: S2.L2, S3.Pin_1, S3.Pin_2, S4.Pin_1, S4.Pin_2, LED2.cathode
